# Fritzing sketch Untitled Sketch 2 (saved by Fritzing 0.9.3b)

parts:
  U2 = ESP8266 NodeMCU LoLin base
  Part2 = BH1750
  LED1 = LEDs [package=led10mm]  # not connected
  Part3 = HC-SR501 Body Sensor Module

nets:
  GND: U2.GND1-3, U2.GND3-1, U2.GND8-0, U2.GND8-5, Part2.GND, Part3.GND
  N1: U2.3V1-3, U2.3V3-2, Part2.VCC
  N2: U2.D0-0, U2.D0-3, Part3.OUT
  N3: U2.D1-0, U2.D1-2, Part2.SCL
  N4: U2.D2-0, U2.D2-2, Part2.SDA
  N5: U2.VUSB-0, Part3.VCC

custom parts:
  ESP8266 NodeMCU LoLin base: ESP8266 based NodeMCU Base
  BH1750: Light Sensor
  LEDs: LEDs Standard schematic elements and footprints for 5mm, 3mm, 1206, and 0603 sized LEDs. 5mm - Spark Fun Electronics SKU : COM-00529 (and others)
  HC-SR501 Body Sensor Module: Pyroelectric Infrared PIR Motion Sensor Detector Module
