# Fritzing sketch Untitled Skฟetch 2 (saved by Fritzing 0.9.3b)

parts:
  U1 = ESP8266 NodeMCU LoLin base
  S1 = H-Bridge with L298N
  Part1 = BH1750 digital light sensor
  Part2 = HC-SR501 Body Sensor Module
  BULB1 = Incandescent light bulb small [package="bulb sm"]

nets:
  GND: U1.GND1-0, U1.GND3-2, U1.GND8-0, U1.GND8-1, S1.GND, Part1.GND, Part2.GND
  N1: U1.3V1-0, U1.3V3-2, Part1.VCC
  N2: U1.D0-0, U1.D0-3, Part2.OUT
  N3: U1.D1-0, Part1.SCL
  N4: U1.D2-0, Part1.SDA
  N5: U1.D3-0, S1.IN2
  N6: U1.D4-0, S1.IN1
  N7: U1.D6-0, S1.ENA
  5V: U1.VUSB-0, U1.VUSB-1, S1.5V, Part2.VCC
  N8: S1.M1-01, BULB1.2
  N9: S1.M1-02, BULB1.1

notes:
  แหล่งจ่ายไฟ

custom parts:
  ESP8266 NodeMCU LoLin base: ESP8266 based NodeMCU Base
  H-Bridge with L298N: h-bridge
  BH1750 digital light sensor: BH1750 digital light sensor SKU: 101222
  HC-SR501 Body Sensor Module: Pyroelectric Infrared PIR Motion Sensor Detector Module
